// Logisim project alu.circ as structural Verilog: 1 circuit, main circuit main
module main (
  input  [31:0] X,
  input  [31:0] Y,
  input  [5:0] Switch__S,
  output Signed_Overflow,
  output [31:0] RESULT,
  output Equal
);

  wire and_2_out, and_3_out, and_4_out, and_5_out, comparator_1_lt, comparator_2_lt, comparator_4_eq,
       comparator_5_lt, comparator_6_eq, comparator_7_eq, not_1_out, not_2_out, not_3_out, not_4_out,
       or_2_out, or_3_out, or_4_out, xnor_1_out, xor_1_out, xor_2_out;
  wire [4:0] bit_extender_1_out;
  wire [31:0] adder_1_out, and_1_out, bit_extender_2_out, bit_extender_3_out, bit_extender_4_out, or_1_out,
       shifter_1_out, shifter_2_out, shifter_3_out, subtractor_1_out;
  wire [31:31] xor_3_out;

  Bit_Extender #(.in_width(32), .out_width(5)) bit_extender_1 (.in(Y), .out(bit_extender_1_out));
  Shifter #(.width(32)) shifter_1 (.in(X), .\dist (bit_extender_1_out), .out(shifter_1_out));
  Shifter #(.width(32), .shift("lr")) shifter_2 (.in(X), .\dist (bit_extender_1_out), .out(shifter_2_out));
  Shifter #(.width(32), .shift("ar")) shifter_3 (.in(X), .\dist (bit_extender_1_out), .out(shifter_3_out));
  Adder #(.width(32)) adder_1 (.a(X), .b(Y), .out(adder_1_out));  // open: cin, cout
  Subtractor #(.width(32)) subtractor_1 (.a(X), .b(Y), .out(subtractor_1_out));  // open: bin, bout
  assign and_1_out = X & Y;  // AND_Gate and_1, 32 bits wide
  assign or_1_out = X | Y;  // OR_Gate or_1, 32 bits wide
  Comparator #(.width(32)) comparator_1 (.a(X), .b(Y), .lt(comparator_1_lt));  // open: gt, eq
  Comparator #(.width(32), .mode("unsigned")) comparator_2 (.a(X), .b(Y), .lt(comparator_2_lt));  // open: gt, eq
  xor xor_1 (xor_1_out, X[3], X[5]);
  Comparator #(.width(32)) comparator_3 (.a(X), .b(Y), .eq(Equal));  // open: gt, lt
  not not_1 (not_1_out, X[31]);
  and and_2 (and_2_out, not_1_out, not_2_out);
  not not_2 (not_2_out, Y[31]);
  and and_3 (and_3_out, X[31], Y[31]);
  assign bit_extender_2_out = {{31{1'b0}}, comparator_1_lt};  // Bit_Extender bit_extender_2
  assign bit_extender_3_out = {{31{1'b0}}, comparator_2_lt};  // Bit_Extender bit_extender_3
  xor xor_2 (xor_2_out, X[2], xor_1_out);
  Comparator #(.width(16)) comparator_4 (
    .a({X[16], X[17], X[18], X[19], X[20], X[21], X[22], X[23], X[24], X[25], X[26], X[27], X[28], X[29], X[30], X[31]}),
    .b(X[15:0]), .eq(comparator_4_eq));  // open: gt, lt
  assign bit_extender_4_out = {{31{1'b0}}, comparator_4_eq};  // Bit_Extender bit_extender_4
  xor xor_3 (xor_3_out[31], X[0], xor_2_out);
  and and_4 (and_4_out, adder_1_out[31], and_2_out);
  not not_3 (not_3_out, adder_1_out[31]);
  not not_4 (not_4_out, Y[31]);
  Comparator #(.width(32)) comparator_5 (.a(X), .b(subtractor_1_out), .lt(comparator_5_lt));  // open: gt, eq
  xnor xnor_1 (xnor_1_out, not_4_out, comparator_5_lt);
  and and_5 (and_5_out, not_3_out, and_3_out);
  or or_2 (or_2_out, and_4_out, and_5_out);
  or or_3 (or_3_out, xnor_1_out, or_2_out);
  and and_6 (Signed_Overflow, or_3_out, or_4_out);
  Multiplexer #(.select(5), .width(32)) multiplexer_1 (
    .in0(shifter_1_out), .in2(shifter_2_out), .in3(shifter_3_out), .in16(adder_1_out), .in17(adder_1_out),
    .in18(subtractor_1_out), .in19(subtractor_1_out), .in20(and_1_out), .in21(or_1_out),
    .in26(bit_extender_2_out), .in27(bit_extender_3_out), .in30(bit_extender_4_out),
    .in31({xor_3_out[31], X[30:0]}), .out(RESULT), .sel({Switch__S[5], Switch__S[3:0]}));  // open: in1, in4, in5, in6, in7, in8, in9, in10, in11, in12, in13, in14, in15, in22, in23, in24, in25, in28, in29, en
  Comparator #(.width(5)) comparator_6 (
    .a(5'b10000), .b({Switch__S[5], Switch__S[3:0]}), .eq(comparator_6_eq));  // open: gt, lt
  Comparator #(.width(5)) comparator_7 (
    .a(5'b10010), .b({Switch__S[5], Switch__S[3:0]}), .eq(comparator_7_eq));  // open: gt, lt
  or or_4 (or_4_out, comparator_6_eq, comparator_7_eq);

  // Notes on the sheet:
  //   INPUTS to your circuit
  //   INPUT to your circuit
  //   DON'T CHANGE THE INPUTS AND OUTPUTS! IF YOU DO SO, YOU NEED TO MAKE SURE THE PINS ARE IN THE RIGHT PLACES!
  //   OUTPUTS of your circuit
endmodule
