// Logisim project cpu.circ as structural Verilog: 6 circuits, main circuit main
module main (
  input  [31:0] RS_READ_VALUE,
  input  [31:0] RT_READ_VALUE,
  input  [31:0] INSTRUCTION,
  input  CLOCK,
  output [31:0] t0,
  output [31:0] t1,
  output [31:0] t2,
  output [31:0] t3,
  output [4:0] RS,
  output [4:0] RT,
  output [4:0] Write_Register,
  output [31:0] RD_WRITE_VALUE,
  output RD_WRITE_ENABLE,
  output [23:0] FETCH_ADDRESS
);

  wire ALU_equal, AluSrc, and_1_out, and_2_out, and_3_out, and_4_out, beq, bne, Branch, branch_t, \byte ,
       comparator_4_eq, comparator_5_eq, LED, MemToReg, not_1_out, OpALU0, OpALU1, pc_1_or_naw, R_Type,
       ReadMem, RegDest, tchecker_2_tcheck, tchecker_3_tcheck, Use_imm, WriteMem;
  wire [1:0] tchecker_1_treg, tchecker_2_treg, tchecker_3_treg;
  wire [5:0] i_type_to_alu_1_func_code, multiplexer_7_out;
  wire [23:0] adder_2_out, bit_extender_1_out, Incremented, multiplexer_1_out, multiplexer_2_out,
       subtractor_1_out;
  wire [31:0] ALU_result, immediate_extender_1_immediate_out, MEM_data_mem_out, multiplexer_5_out,
       multiplexer_6_out, RegFile_read_data_1, RegFile_read_data_2, RT_t;

  Adder #(.width(24)) adder_1 (.a(FETCH_ADDRESS), .b(24'h1), .out(Incremented));  // open: cin, cout
  Multiplexer #(.width(24)) multiplexer_1 (
    .in0(Incremented), .in1(adder_2_out), .out(multiplexer_1_out), .sel(branch_t));  // open: en
  assign bit_extender_1_out = {{8{1'b0}}, INSTRUCTION[15:0]};  // Bit_Extender bit_extender_1
  Subtractor #(.width(24)) subtractor_1 (
    .a(INSTRUCTION[23:0]), .b(24'h100000), .out(subtractor_1_out));  // open: bin, bout
  Adder #(.width(24)) adder_2 (.a(FETCH_ADDRESS), .b(bit_extender_1_out), .out(adder_2_out));  // open: cin, cout
  Multiplexer #(.width(24)) multiplexer_2 (
    .in0(multiplexer_1_out), .in1(subtractor_1_out), .out(multiplexer_2_out), .sel(pc_1_or_naw));  // open: en
  Register #(.width(24)) PC (.D(multiplexer_2_out), .Q(FETCH_ADDRESS), .clk(CLOCK));  // open: en, clr
  TChecker tchecker_1 (.in_1(INSTRUCTION[25:21]), .TReg(tchecker_1_treg));  // open: TCheck
  TChecker tchecker_2 (.in_1(INSTRUCTION[20:16]), .TCheck(tchecker_2_tcheck), .TReg(tchecker_2_treg));
  Multiplexer #(.width(5)) multiplexer_3 (
    .in0(INSTRUCTION[20:16]), .in1(INSTRUCTION[15:11]), .out(Write_Register), .sel(RegDest));  // open: en
  TChecker tchecker_3 (.in_1(Write_Register), .TCheck(tchecker_3_tcheck), .TReg(tchecker_3_treg));
  regfile_main RegFile (
    .Read_register_1(tchecker_1_treg), .Read_register_2(tchecker_2_treg), .write_register(tchecker_3_treg),
    .write_data(RD_WRITE_VALUE), .t0_Value(t0), .t1_Value(t1), .t2_Value(t2), .t3_Value(t3),
    .RegWrite(and_1_out), .clock(CLOCK), .Read_Data_1(RegFile_read_data_1), .Read_Data_2(RegFile_read_data_2));
  and and_1 (and_1_out, RD_WRITE_ENABLE, tchecker_3_tcheck);
  Immediate_Extender immediate_extender_1 (
    .opcode_in(INSTRUCTION[31:26]), .immediate_in(INSTRUCTION[15:0]), .shift_amount(INSTRUCTION[10:6]),
    .immediate_out(immediate_extender_1_immediate_out));
  Multiplexer #(.width(32)) multiplexer_4 (
    .in0(RT_READ_VALUE), .in1(RegFile_read_data_2), .out(RT_t), .sel(tchecker_2_tcheck));  // open: en
  Comparator #(.width(6)) comparator_1 (.a(6'b000101), .b(INSTRUCTION[31:26]), .eq(bne));  // open: gt, lt
  Comparator #(.width(6)) comparator_2 (.a(6'b000100), .b(INSTRUCTION[31:26]), .eq(beq));  // open: gt, lt
  Comparator #(.width(6)) comparator_3 (.a({6{1'b0}}), .b(INSTRUCTION[31:26]), .eq(R_Type));  // open: gt, lt
  Use_Immediate use_immediate_1 (.in_1(INSTRUCTION[31:26]), .in_2(INSTRUCTION[5:0]), .Operation(Use_imm));
  and and_2 (and_2_out, R_Type, LED);
  LED led_1 (.in(and_2_out));
  Multiplexer #(.width(32)) multiplexer_5 (
    .in0(RS_READ_VALUE), .in1(RegFile_read_data_1), .out(multiplexer_5_out), .sel(tchecker_2_tcheck));  // open: en
  Multiplexer #(.width(32)) multiplexer_6 (
    .in0(RT_t), .in1(immediate_extender_1_immediate_out), .out(multiplexer_6_out), .sel(Use_imm));  // open: en
  alu_main ALU (
    .Switch__S(multiplexer_7_out), .X(multiplexer_5_out), .Equal(ALU_equal), .RESULT(ALU_result),
    .Signed_Overflow(LED), .Y(multiplexer_6_out));
  Multiplexer #(.width(6)) multiplexer_7 (
    .in0(i_type_to_alu_1_func_code), .in1(INSTRUCTION[5:0]), .out(multiplexer_7_out), .sel(R_Type));  // open: en
  not not_1 (not_1_out, ALU_equal);
  I_type_to_ALU i_type_to_alu_1 (.opcode(INSTRUCTION[31:26]), .Func_Code(i_type_to_alu_1_func_code));
  Comparator #(.width(6)) comparator_4 (.a(6'b100100), .b(INSTRUCTION[31:26]), .eq(comparator_4_eq));  // open: gt, lt
  Comparator #(.width(6)) comparator_5 (.a(6'b100000), .b(INSTRUCTION[31:26]), .eq(comparator_5_eq));  // open: gt, lt
  and and_3 (and_3_out, not_1_out, bne);
  and and_4 (and_4_out, ALU_equal, beq);
  or or_1 (branch_t, and_3_out, and_4_out);
  or or_2 (\byte , comparator_4_eq, comparator_5_eq);
  mem_main MEM (
    .Data_Mem_Addr(ALU_result), .Data_Mem_In(RT_t), .ACCESS_BYTE(\byte ), .MEM_WRITE(WriteMem),
    .CLOCK(CLOCK), .Data_Mem_Out(MEM_data_mem_out));
  control control_1 (
    .OPcode(INSTRUCTION[31:26]), .RegDst(RegDest), .ALUSrc(AluSrc), .MemToReg(MemToReg),
    .WriteReg(RD_WRITE_ENABLE), .ReadMem(Branch), .WriteMem(WriteMem), .Branch(ReadMem), .OpALU1(OpALU1),
    .OpALU0(OpALU0));
  Multiplexer #(.width(32)) multiplexer_8 (
    .in0(ALU_result), .in1(MEM_data_mem_out), .out(RD_WRITE_VALUE), .sel(MemToReg));  // open: en

  assign RS = INSTRUCTION[25:21];
  assign RT = INSTRUCTION[20:16];

  // Other names for the same wires on the sheet: clk = CLOCK; address[25:0] = INSTRUCTION[25:0];
  //   function[5:0] = INSTRUCTION[5:0]; immediate[15:0] = INSTRUCTION[15:0];
  //   word_addressed_target[23:0] = INSTRUCTION[23:0]; shift_amount[4:0] = INSTRUCTION[10:6];
  //   register_d[4:0] = INSTRUCTION[15:11]; register_t[4:0] = INSTRUCTION[20:16];
  //   register_s[4:0] = INSTRUCTION[25:21]; opcode[5:0] = INSTRUCTION[31:26]; S[31:0] = RS_READ_VALUE;
  //   store_register[4:0] = Write_Register; T[31:0] = RT_READ_VALUE; WriteReg = RD_WRITE_ENABLE

  // Notes on the sheet:
  //   These are outputs/inputs from run.circ
  //   These are outputs to run.circ
endmodule

module control (
  input  [5:0] OPcode,
  output RegDst,
  output ALUSrc,
  output MemToReg,
  output WriteReg,
  output ReadMem,
  output WriteMem,
  output Branch,
  output OpALU1,
  output OpALU0
);

  wire not_1_out, not_2_out, not_3_out, not_4_out, not_5_out, not_6_out, not_7_out, not_8_out, not_9_out,
       not_10_out, not_11_out, not_12_out, not_13_out, not_14_out, not_15_out, not_16_out;

  not not_1 (not_1_out, OPcode[4]);
  not not_2 (not_2_out, OPcode[2]);
  not not_3 (not_3_out, OPcode[0]);
  not not_4 (not_4_out, OPcode[5]);
  not not_5 (not_5_out, OPcode[3]);
  not not_6 (not_6_out, OPcode[1]);
  and and_1 (OpALU1, not_4_out, not_1_out, not_5_out, not_2_out, not_6_out, not_3_out);
  not not_7 (not_7_out, OPcode[4]);
  not not_8 (not_8_out, OPcode[3]);
  not not_9 (not_9_out, OPcode[2]);
  and and_2 (MemToReg, OPcode[5], not_7_out, not_8_out, not_9_out, OPcode[1], OPcode[0]);
  not not_10 (not_10_out, OPcode[4]);
  not not_11 (not_11_out, OPcode[2]);
  and and_3 (WriteMem, OPcode[5], not_10_out, OPcode[3], not_11_out, OPcode[1], OPcode[0]);
  not not_12 (not_12_out, OPcode[5]);
  not not_13 (not_13_out, OPcode[4]);
  not not_14 (not_14_out, OPcode[0]);
  not not_15 (not_15_out, OPcode[1]);
  not not_16 (not_16_out, OPcode[3]);
  and and_4 (Branch, not_12_out, not_13_out, not_16_out, OPcode[2], not_15_out, not_14_out);
  or or_1 (ALUSrc, MemToReg, WriteMem);
  or or_2 (WriteReg, OpALU1, MemToReg);

  assign OpALU0 = Branch;
  assign ReadMem = MemToReg;
  assign RegDst = OpALU1;
endmodule

module Immediate_Extender (
  input  [5:0] opcode_in,
  input  [4:0] shift_amount,
  input  [15:0] immediate_in,
  output [31:0] immediate_out
);

  wire comparator_1_eq, comparator_2_eq, comparator_3_eq, comparator_4_eq;
  wire [1:0] or_1_out;
  wire [31:0] bit_extender_1_out, bit_extender_2_out, bit_extender_3_out, bit_extender_4_out,
       multiplexer_1_out, multiplexer_2_out;

  Comparator #(.width(6)) comparator_1 (.a(opcode_in), .b(6'b001000), .eq(comparator_1_eq));  // open: gt, lt
  Comparator #(.width(6)) comparator_2 (.a(opcode_in), .b(6'b001001), .eq(comparator_2_eq));  // open: gt, lt
  Comparator #(.width(6)) comparator_3 (.a(opcode_in), .b(6'b001101), .eq(comparator_3_eq));  // open: gt, lt
  Comparator #(.width(6)) comparator_4 (.a(opcode_in), .b(6'b001111), .eq(comparator_4_eq));  // open: gt, lt
  Comparator #(.width(6)) comparator_5 (.a(opcode_in), .b({6{1'b0}}), .eq(or_1_out[1]));  // open: gt, lt
  or or_1 (or_1_out[0], comparator_1_eq, comparator_2_eq, comparator_3_eq);
  assign bit_extender_1_out = {{16{immediate_in[15]}}, immediate_in};  // Bit_Extender bit_extender_1
  assign bit_extender_2_out = {{16{1'b0}}, immediate_in};  // Bit_Extender bit_extender_2
  assign bit_extender_3_out = {{16{1'b0}}, immediate_in};  // Bit_Extender bit_extender_3
  Multiplexer #(.width(32)) multiplexer_1 (
    .in0(bit_extender_1_out), .in1(bit_extender_2_out), .out(multiplexer_1_out), .sel(comparator_3_eq));  // open: en
  assign bit_extender_4_out = {{27{1'b0}}, shift_amount};  // Bit_Extender bit_extender_4
  Multiplexer #(.width(32)) multiplexer_2 (
    .in0(bit_extender_3_out), .in1(32'h10), .out(multiplexer_2_out), .sel(comparator_4_eq));  // open: en
  Multiplexer #(.select(2), .width(32)) multiplexer_3 (
    .in0(multiplexer_2_out), .in1(multiplexer_1_out), .in2(bit_extender_4_out), .out(immediate_out),
    .sel(or_1_out));  // open: in3, en
endmodule

module TChecker (
  input  [4:0] in_1,
  output TCheck,
  output [1:0] TReg
);

  wire comparator_1_lt, comparator_2_gt;
  wire [4:0] subtractor_1_out;

  Comparator #(.width(5), .mode("unsigned")) comparator_1 (
    .a(in_1), .b(5'b01011), .lt(comparator_1_lt));  // open: gt, eq
  Comparator #(.width(5)) comparator_2 (.a(in_1), .b(5'b01000), .gt(comparator_2_gt));  // open: eq, lt
  Subtractor #(.width(5)) subtractor_1 (.a(in_1), .b(5'b01000), .out(subtractor_1_out));  // open: bin, bout
  and and_1 (TCheck, comparator_1_lt, comparator_2_gt);
  Bit_Extender #(.in_width(5), .out_width(2)) bit_extender_1 (.in(subtractor_1_out), .out(TReg));
endmodule

module Use_Immediate (
  input  [5:0] in_1,
  input  [5:0] in_2,
  output Operation
);

  wire and_1_out, and_2_out, and_3_out, comparator_1_eq, comparator_2_eq, comparator_3_eq, comparator_4_eq,
       comparator_5_eq, comparator_6_eq, comparator_7_eq, comparator_8_eq;

  Comparator #(.width(6)) comparator_1 (.a(in_1), .b({6{1'b0}}), .eq(comparator_1_eq));  // open: gt, lt
  Comparator #(.width(6)) comparator_2 (.a(in_1), .b(6'b001000), .eq(comparator_2_eq));  // open: gt, lt
  Comparator #(.width(6)) comparator_3 (.a(in_1), .b(6'b001001), .eq(comparator_3_eq));  // open: gt, lt
  Comparator #(.width(6)) comparator_4 (.a(in_1), .b(6'b001101), .eq(comparator_4_eq));  // open: gt, lt
  Comparator #(.width(6)) comparator_5 (.a(in_1), .b(6'b001111), .eq(comparator_5_eq));  // open: gt, lt
  Comparator #(.width(6)) comparator_6 (.a(in_2), .b({6{1'b0}}), .eq(comparator_6_eq));  // open: gt, lt
  Comparator #(.width(6)) comparator_7 (.a(in_2), .b(6'b000010), .eq(comparator_7_eq));  // open: gt, lt
  Comparator #(.width(6)) comparator_8 (.a(in_2), .b(6'b000011), .eq(comparator_8_eq));  // open: gt, lt
  and and_1 (and_1_out, comparator_6_eq, comparator_1_eq);
  and and_2 (and_2_out, comparator_1_eq, comparator_7_eq);
  and and_3 (and_3_out, comparator_1_eq, comparator_8_eq);
  or or_1 (Operation, and_1_out, and_2_out, comparator_2_eq, comparator_3_eq, comparator_4_eq, comparator_5_eq);
endmodule

module I_type_to_ALU (
  input  [5:0] opcode,
  output [5:0] Func_Code
);

  Multiplexer #(.select(5), .width(6)) multiplexer_1 (
    .in0(6'b100001), .in3(6'b100001), .in4(6'b100001), .in8(6'b100000), .in9(6'b100001), .in11(6'b100001),
    .in13(6'b100101), .in15({6{1'b0}}), .out(Func_Code), .sel(opcode[4:0]));  // open: in1, in2, in5, in6, in7, in10, in12, in14, in16, in17, in18, in19, in20, in21, in22, in23, in24, in25, in26, in27, in28, in29, in30, in31, en
endmodule
